# Fritzing sketch ultimate_altimeter_prototype_1 (saved by Fritzing 0.9.3b)
breadboards: 1

parts:
  Part1 = Altitude/Pressure Sensor - MPL3115A2 Breakout [part_number=SEN-11084]
  R1 = Resistor [tolerance=±5% resistance=330 package="2512 [SMD]"]
  R2 = Resistor [tolerance=±5% resistance=330 package="2512 [SMD]"]
  Parts1 = SparkFun RedBoard [part_number=DEV-12757]
  Representing_the_Electric_Imp_Shield = Arduino WiFly Shield

nets:
  N1: Part1.SDA, R2.Pin_1
  N2: Part1.SCL, R1.Pin_1
  VCC: Part1.VCC, Parts1.3V3, Representing_the_Electric_Imp_Shield.VIN
  GND: Part1.GND, Parts1.GND, Representing_the_Electric_Imp_Shield.GND
  N3: R1.Pin_0, Parts1.A5/SCL
  N4: R2.Pin_0, Parts1.A4/SDA

custom parts:
  SparkFun RedBoard: At SparkFun we use many Arduinos and we’re always looking for the simplest, most stable one. Each board is a bit different and no one board has everything we want, so we decided to make our own version that combines all our favorite features. The RedBoard combines the simplicity of the UNO’s Optiboot bootloader (which is used in the Pro series), the stability of the FTDI (which we all missed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
